# Fritzing sketch SmartHousePlantWateringsys (saved by Fritzing 1.0.2b)
breadboards: 3

parts:
  Breadboard4 = Breadboard Split Power
  Breadboard5 = Breadboard Split Power
  OLED_I2C1 = OLED 128x64 I2C Monochrome Display
  Part1 = MQ-131 breakout
  Grove1 = Grove Dust Sensor
  R1 = Resistor [tolerance=±5% power=0.25W resistance=220 package=THT]
  R2 = Resistor [tolerance=±5% power=0.25W resistance=2200 package=THT]
  Q1 = PNP-Transistor [package="TO92 [THT]"]
  Relay1 = Relay - 6 pins [package="DIP (Dual Inline) [THT]"]
  WATER_PUMP1 = water pump/motor  # not connected
  Part2 = BME280 Breakout
  A1 = Particle - Photon2
  SENS1 = SoilWatch 10

nets (from the schematic view):
  N1: Breadboard4.pin17Y, Breadboard4.pin22Y, Breadboard4.pin29Y
  N2: Breadboard4.pin20Z, Breadboard4.pin29Z
  N3: Breadboard5.pin3Y, Breadboard5.pin15Y
  N4: Breadboard5.pin3Z, Breadboard5.pin28Z
  N5: Breadboard5.pin17Y, Breadboard5.pin29Y
  N6: OLED_I2C1.SDA, Part2.SDI/SDA, A1.Pin_17
  N7: OLED_I2C1.SCK, Part2.SCK/SCL, A1.Pin_18
  VCC: OLED_I2C1.VDD, Part1.VCC, Relay1.VCC, Part2.3.3V, A1.Pin_2, A1.Pin_31, SENS1.VCC
  N8: OLED_I2C1.GND, Relay1.ON, A1.Pin_4, A1.Pin_21, A1.Pin_30, A1.Pin_35
  N9: Part1.AO, A1.Pin_5
  GND: Grove1.GND, Relay1.GND, Part2.GND
  N10: Grove1.VCC, R1.Pin_0
  N11: Grove1.NC#5, A1.Pin_20
  N12: R1.Pin_1, Relay1.IN
  N13: R2.Pin_1, Q1.B, SENS1.GND
  N14: A1.Pin_7, SENS1.OUT

custom parts:
  Breadboard Split Power: A custom 6 pin per group power supply strip where the top row (ground) is all bussed together and the bottom row (+V) is split in two groups of 12 pins. This version is modified to be a loadable part and was rescaled to be on the standard 1px = 1thou grid with the size set in inches
  MQ-131 breakout: SKU: 101282
  Grove Dust Sensor: PPD42 Grove Dust Sensor
  Relay - 6 pins: A DIP stand-in part for whatever IC you want. With 6 pins on a 900mil dual inline package (DIP) footprint.
  water pump/motor: WATER PUMP BY ARDUBLOCKTR
  Particle - Photon2: The Photon 2 is a microcontroller and Wi-Fi networking developed by particle. Features: 802.11a/b/g/n Wi-Fi, 2.4 GHz and 5 GHz Integrated PCB antenna Integrated U.FL connector for external antenna Integrated RF switch BLE 5 using same antenna as Wi-Fi Realtek RTL8721DM MCU ARM Cortex M33 CPU, 200 MHz 2048 KB (2 MB) user application maximum size 3072 KB (3 MB) of RAM available to user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
  SoilWatch 10: SoilWatch 10 - Capacitive soil moisture sensor
